# Fritzing sketch DHT11 (saved by Fritzing 0.9.3b)

parts:
  DHT1 = DHT11 Humitidy and Temperature Sensor (3 pins)
  Part1 = Arduino Uno (Rev3)

nets:
  N1: DHT1.DATA, Part1.D2
  VDD: DHT1.VDD, Part1.5V
  GND: DHT1.GND, Part1.GND

custom parts:
  DHT11 Humitidy and Temperature Sensor (3 pins): DHT11 Humidity and Temperature Sensor (3 pins) from the design created by John De Cristofaro for Adafruit Industries.
