# Fritzing sketch Untitled Sketch 2 (saved by Fritzing 0.9.3b)
breadboards: 1

parts:
  Part1 = SRF05 Ultrasonic Rangefinder
  DHT2 = DHT11 Humitidy and Temperature Sensor (3 pins)
  YF-S201_Flow_Meter2 = YF-S201 Water Flow Meter
  Part2 = Arduino Uno (Rev3)
  U1 = NodeMCU V1.0

nets:
  VCC: Part1.VCC, U1.Vin
  N1: Part1.Trig, U1.D4
  N2: Part1.Echo, U1.D3
  GND: Part1.GND, DHT2.GND, YF-S201_Flow_Meter2.GND, Part2.GND, U1.GND
  N3: DHT2.DATA, Part2.AREF, U1.3V3
  N4: DHT2.VDD, U1.D1
  N5: YF-S201_Flow_Meter2.SIG, Part2.D2
  VCC_2: YF-S201_Flow_Meter2.VCC, Part2.3V3

custom parts:
  DHT11 Humitidy and Temperature Sensor (3 pins): DHT11 Humidity and Temperature Sensor (3 pins) from the design created by John De Cristofaro for Adafruit Industries.
  YF-S201 Water Flow Meter: The YF-S201 Flow Meter. The input voltage is 5V to 24V (DC).
  NodeMCU V1.0: ESP8266 based NodeMCU
